# Fritzing sketch diagram (saved by Fritzing 0.7.11b)
breadboards: 1

parts:
  IC1 = IC, DIP package, 20 pins [chip_label=74LS245]
  IC2 = IC, DIP package, 20 pins [chip_label=74LS245]
  IC3 = IC, DIP package, 20 pins [chip_label=74LS245]
  IC4 = IC, DIP package, 20 pins [chip_label=74LS245]
  LAYER_1 = LED - 5mm [color="Red (633nm)" package="5 mm [THT]"]  # not connected
  LED2 = LED - 5mm [color="Red (633nm)" package="5 mm [THT]"]  # not connected
  LED3 = LED - 5mm [color="Red (633nm)" package="5 mm [THT]"]  # not connected
  LED4 = LED - 5mm [color="Red (633nm)" package="5 mm [THT]"]
  LED5 = LED - 5mm [color="Red (633nm)" package="5 mm [THT]"]  # not connected
  LED6 = LED - 5mm [color="Red (633nm)" package="5 mm [THT]"]  # not connected
  LED7 = LED - 5mm [color="Red (633nm)" package="5 mm [THT]"]  # not connected
  LED8 = LED - 5mm [color="Red (633nm)" package="5 mm [THT]"]
  LED9 = LED - 5mm [color="Red (633nm)" package="5 mm [THT]"]  # not connected
  LED10 = LED - 5mm [color="Red (633nm)" package="5 mm [THT]"]  # not connected
  LED11 = LED - 5mm [color="Red (633nm)" package="5 mm [THT]"]
  LED12 = LED - 5mm [color="Red (633nm)" package="5 mm [THT]"]  # not connected
  LED13 = LED - 5mm [color="Red (633nm)" package="5 mm [THT]"]
  LED14 = LED - 5mm [color="Red (633nm)" package="5 mm [THT]"]
  LED15 = LED - 5mm [color="Red (633nm)" package="5 mm [THT]"]
  LED16 = LED - 5mm [color="Red (633nm)" package="5 mm [THT]"]
  LED17 = LED - 5mm [color="Red (633nm)" package="5 mm [THT]"]  # not connected
  LED18 = LED - 5mm [color="Red (633nm)" package="5 mm [THT]"]  # not connected
  LED19 = LED - 5mm [color="Red (633nm)" package="5 mm [THT]"]
  LAYER_2 = LED - 5mm [color="Red (633nm)" package="5 mm [THT]"]  # not connected
  LED21 = LED - 5mm [color="Red (633nm)" package="5 mm [THT]"]  # not connected
  LED22 = LED - 5mm [color="Red (633nm)" package="5 mm [THT]"]
  LED23 = LED - 5mm [color="Red (633nm)" package="5 mm [THT]"]  # not connected
  LED24 = LED - 5mm [color="Red (633nm)" package="5 mm [THT]"]  # not connected
  LED25 = LED - 5mm [color="Red (633nm)" package="5 mm [THT]"]
  LED26 = LED - 5mm [color="Red (633nm)" package="5 mm [THT]"]  # not connected
  LED27 = LED - 5mm [color="Red (633nm)" package="5 mm [THT]"]
  LED28 = LED - 5mm [color="Red (633nm)" package="5 mm [THT]"]
  LED29 = LED - 5mm [color="Red (633nm)" package="5 mm [THT]"]  # not connected
  LED30 = LED - 5mm [color="Red (633nm)" package="5 mm [THT]"]  # not connected
  LED31 = LED - 5mm [color="Red (633nm)" package="5 mm [THT]"]
  LED32 = LED - 5mm [color="Red (633nm)" package="5 mm [THT]"]
  LED33 = LED - 5mm [color="Red (633nm)" package="5 mm [THT]"]  # not connected
  LED34 = LED - 5mm [color="Red (633nm)" package="5 mm [THT]"]  # not connected
  LED35 = LED - 5mm [color="Red (633nm)" package="5 mm [THT]"]  # not connected
  LED36 = LED - 5mm [color="Red (633nm)" package="5 mm [THT]"]
  LAYER_3 = LED - 5mm [color="Red (633nm)" package="5 mm [THT]"]  # not connected
  LAYER_4 = LED - 5mm [color="Red (633nm)" package="5 mm [THT]"]  # not connected
  LED39 = LED - 5mm [color="Red (633nm)" package="5 mm [THT]"]  # not connected
  LED40 = LED - 5mm [color="Red (633nm)" package="5 mm [THT]"]  # not connected
  LED41 = LED - 5mm [color="Red (633nm)" package="5 mm [THT]"]
  LED42 = LED - 5mm [color="Red (633nm)" package="5 mm [THT]"]  # not connected
  LED43 = LED - 5mm [color="Red (633nm)" package="5 mm [THT]"]  # not connected
  LED44 = LED - 5mm [color="Red (633nm)" package="5 mm [THT]"]  # not connected
  LED45 = LED - 5mm [color="Red (633nm)" package="5 mm [THT]"]  # not connected
  LED46 = LED - 5mm [color="Red (633nm)" package="5 mm [THT]"]  # not connected
  LED47 = LED - 5mm [color="Red (633nm)" package="5 mm [THT]"]
  LED48 = LED - 5mm [color="Red (633nm)" package="5 mm [THT]"]
  LED49 = LED - 5mm [color="Red (633nm)" package="5 mm [THT]"]
  LED50 = LED - 5mm [color="Red (633nm)" package="5 mm [THT]"]  # not connected
  LED51 = LED - 5mm [color="Red (633nm)" package="5 mm [THT]"]
  LED52 = LED - 5mm [color="Red (633nm)" package="5 mm [THT]"]  # not connected
  LED53 = LED - 5mm [color="Red (633nm)" package="5 mm [THT]"]
  LED54 = LED - 5mm [color="Red (633nm)" package="5 mm [THT]"]  # not connected
  LED55 = LED - 5mm [color="Red (633nm)" package="5 mm [THT]"]
  LED56 = LED - 5mm [color="Red (633nm)" package="5 mm [THT]"]
  LED57 = LED - 5mm [color="Red (633nm)" package="5 mm [THT]"]
  LED58 = LED - 5mm [color="Red (633nm)" package="5 mm [THT]"]  # not connected
  LED59 = LED - 5mm [color="Red (633nm)" package="5 mm [THT]"]
  LED60 = LED - 5mm [color="Red (633nm)" package="5 mm [THT]"]
  LED61 = LED - 5mm [color="Red (633nm)" package="5 mm [THT]"]
  LED62 = LED - 5mm [color="Red (633nm)" package="5 mm [THT]"]  # not connected
  LED63 = LED - 5mm [color="Red (633nm)" package="5 mm [THT]"]  # not connected
  LED64 = LED - 5mm [color="Red (633nm)" package="5 mm [THT]"]
  Arduino1 = Arduino
  R1 = Photocell (LDR) [package=THT]
  R2 = 10k Ω Resistor [package=THT]

nets:
  N1: IC1.pin1, IC1.pin20, IC2.pin1, IC2.pin20, IC3.pin1, IC3.pin20, IC4.pin1, IC4.pin20, Arduino1.+5V, R2.Pin_1
  N2: IC1.pin2, IC2.pin2, IC3.pin2, IC4.pin2, Arduino1.D9
  N3: IC1.pin3, IC2.pin3, IC3.pin3, IC4.pin3, Arduino1.D8
  N4: IC1.pin4, IC2.pin4, IC3.pin4, IC4.pin4, Arduino1.D7
  N5: IC1.pin5, IC2.pin5, IC3.pin5, IC4.pin5, Arduino1.D6
  N6: IC1.pin6, IC2.pin6, IC3.pin6, IC4.pin6, Arduino1.D5
  N7: IC1.pin7, IC2.pin7, IC3.pin7, IC4.pin7, Arduino1.D4
  N8: IC1.pin8, IC2.pin8, IC3.pin8, IC4.pin8, Arduino1.D3
  N9: IC1.pin9, IC2.pin9, IC3.pin9, IC4.pin9, Arduino1.D2
  N10: IC1.pin10, IC2.pin10, IC3.pin10, IC4.pin10, Arduino1.GND, R1.pin_0
  N11: IC1.pin11, LED4.cathode
  N12: IC1.pin12, LED8.cathode
  N13: IC1.pin13, LED11.cathode
  N14: IC1.pin14, LED15.cathode
  N15: IC1.pin15, LED15.anode
  N16: IC1.pin16, LED14.anode
  N17: IC1.pin17, LED16.anode
  N18: IC1.pin18, LED13.anode
  N19: IC1.pin19, Arduino1.A0
  N20: IC2.pin11, LED61.cathode
  N21: IC2.pin12, LED60.cathode
  N22: IC2.pin13, LED49.cathode
  N23: IC2.pin14, LED57.cathode
  N24: IC2.pin15, LED57.anode
  N25: IC2.pin16, LED41.anode
  N26: IC2.pin17, LED56.anode
  N27: IC2.pin18, LED47.anode
  N28: IC2.pin19, Arduino1.A3
  N29: IC3.pin11, LED64.cathode
  N30: IC3.pin12, LED55.cathode
  N31: IC3.pin13, LED59.cathode
  N32: IC3.pin14, LED51.cathode
  N33: IC3.pin15, LED51.anode
  N34: IC3.pin16, LED48.anode
  N35: IC3.pin17, LED53.anode
  N36: IC3.pin18, LED36.anode
  N37: IC3.pin19, Arduino1.A2
  N38: IC4.pin11, LED28.cathode
  N39: IC4.pin12, LED32.cathode
  N40: IC4.pin13, LED27.cathode
  N41: IC4.pin14, LED25.cathode
  N42: IC4.pin15, LED25.anode
  N43: IC4.pin16, LED22.anode
  N44: IC4.pin17, LED31.anode
  N45: IC4.pin18, LED19.anode
  N46: IC4.pin19, Arduino1.A1
  N47: Arduino1.A4, R1.pin_1, R2.Pin_0
